# Fritzing sketch hw_module (saved by Fritzing 0.9.3b)

parts:
  MCU1 = Wemos Lolin32lite
  BAT1 = 18650 battery holder [package=battery-18650-kit]
  S1 = Toggle Switch [package=THT]
  S2 = Round Pushbutton
  R2 = Resistor [tolerance=±5% resistance=10k package="0805 [SMD]"]
  R3 = Trimmer Potentiometer [maximum_resistance=10kΩ package=THT]
  R4 = Trimmer Potentiometer [maximum_resistance=10kΩ package=THT]
  R1 = Resistor [tolerance=±5% resistance=10k package="0805 [SMD]"]
  R5 = Trimmer Potentiometer [maximum_resistance=10kΩ package=THT]
  R6 = Trimmer Potentiometer [maximum_resistance=10kΩ package=THT]
  R7 = Trimmer Potentiometer [maximum_resistance=10kΩ package=THT]
  Amperemeter1 = Amperemeter  # not connected
  Voltmeter2 = Voltmeter  # not connected
  Voltmeter3 = Voltmeter  # not connected
  Voltmeter4 = Voltmeter  # not connected
  Voltmeter5 = Voltmeter  # not connected
  Voltmeter6 = Voltmeter  # not connected
  Voltmeter7 = Voltmeter  # not connected
  Amperemeter2 = Amperemeter  # not connected
  Amperemeter3 = Amperemeter  # not connected
  Voltmeter1 = Voltmeter  # not connected

nets:
  N1: MCU1.pin_3, S2.leg1
  N2: MCU1.pin_16, R1.Pin_0
  N3: MCU1.pin_17, R2.Pin_0
  N4: MCU1.pin_18, R7.leg1
  N5: BAT1.-, S1.L1
  N6: R2.Pin_1, R3.leg1, R3.wiper
  N7: R3.leg2, R5.leg1
  N8: R4.leg1, R4.wiper, R1.Pin_1
  N9: R4.leg2, R6.leg1

notes:
  10kOhm smd res
  <- 50kOhm pot
  10kOhm precision pot ->
  5kOhm precision pot ->
  uAmmeter RAM
  uAmmeter HDD
  mAmmeter CORE01
  Voltmeter CORE02
  Voltmeter CORE03
  Voltmeter CORE04
  Voltmeter CORE05
  Voltmeter CORE06
  Voltmeter CORE07
  Voltmeter CORE08

custom parts:
  Wemos Lolin32lite: Wemos Lolinlite32 wifi and blue tooth board based on the ESP-32 cpu, digital I/Os 19, analog inputs 6, clock 240mhz, Flash 4Mbytes, lipo battery charger (500ma connection broken out on breadboard but not pcb), usb.
  18650 battery holder: 18650 Battery Holder
  Amperemeter: A Standard Multimeter in Current mode
  Voltmeter: A Standard Multimeter in Current mode
